# Fritzing sketch Door Pi (saved by Fritzing 0.9.4)
circuit board: 8.53488cm x 5.63626cm
breadboards: 1

parts:
  12V_LED = LEDs [package=led10mm]
  J10 = Raspberry Pi Header 40pin [package=THT]
  Strike_Relay = AQT212GH [package="DIP (Dual Inline) [THT]"]
  Bell_Relay = AQT212GH [package="DIP (Dual Inline) [THT]"]
  Led1 = l710a8ge dual led [package=THT]
  LLC2 = Logic Level Converter [package="Breakout board"]
  U6 = TSR2 Series
  12V1 = 2.1mm DC Barrel Jack
  Fuse2 = Fuse with Handler [part_number=Htc-15m]
  Door_Reader = Camdenboss CTB0158-8 [package=THT]
  Door_Strike = Camdenboss CTB0158-2 [package=THT]
  DoorBell = Camdenboss CTB0158-2 [package=THT]
  R3 = Resistor [tolerance=±5% resistance=470 package=THT]
  R2 = Resistor [tolerance=±5% resistance=470 package=THT]
  Door_Sensor = Camdenboss CTB0158-2 [package=THT]
  Led2 = l710a8ge dual led [package=THT]
  R4 = Resistor [tolerance=±5% resistance=470 package=THT]
  R5 = Resistor [tolerance=±5% resistance=470 package=THT]

nets:
  GND: 12V_LED.C, J10.GND, Strike_Relay.pin1, Bell_Relay.pin1, Led1.pin1, Led1.pin3, LLC2.L-GND, LLC2.H-GND, U6.GND, 12V1.GND, 12V1.sleeve, Door_Reader.pin2, Door_Strike.pin1, DoorBell.pin1, Led2.pin1, Led2.pin3
  N1: 12V_LED.A, Strike_Relay.pin4, Bell_Relay.pin4, 12V1.center_(V+), Fuse2.Connector2, Door_Reader.pin1
  N2: J10.3V3, LLC2.LV, Door_Reader.pin7, Door_Sensor.pin1
  N3: J10.5V, LLC2.HV, U6.OUT
  N4: J10.IO4, Strike_Relay.pin2
  N5: J10.IO14, LLC2.LV2
  N6: J10.IO15, LLC2.LV1
  N7: J10.IO17, Bell_Relay.pin2
  N8: J10.IO22#12, LLC2.LV3
  N9: J10.IO22#14, LLC2.LV4
  N10: J10.IO5, Door_Reader.pin8
  N11: J10.IO6, Door_Sensor.pin2
  N12: J10.IO13, R5.Pin_0
  N13: J10.IO19, R4.Pin_1
  N14: Strike_Relay.pin3, Door_Strike.pin2, R2.Pin_0
  N15: Bell_Relay.pin3, DoorBell.pin2, R3.Pin_0
  N16: Led1.pin2, R3.Pin_1
  N17: Led1.pin4, R2.Pin_1
  N18: LLC2.HV4, Door_Reader.pin6
  N19: LLC2.HV3, Door_Reader.pin5
  N20: LLC2.HV2, Door_Reader.pin4
  N21: LLC2.HV1, Door_Reader.pin3
  N22: U6.IN, Fuse2.Connector1

notes:
  5V
  12V
  3.3V

custom parts:
  Raspberry Pi Header 40pin: Raspberry Pi 40 pin header - for creating your own shields. (Mar 2020, bb: make breadboard friendly (.4in pin spacing) and add labels. Schematic add labels. PCB make oblong pins to allow routing traces between the pins.)
  AQT212GH: PhotoMOS GU 1 Form A High Capacity opto isolator. 4-pin high capacity of 1.1A, I/O isolation voltage of 5,000V
  l710a8ge dual led: KingBright L-710A8GE/11GD-RV T-1 (3mm) BI-LEVEL LED INDICATOR red/green.
  Logic Level Converter: 5V to/from 3.3V logic level converter
  TSR2 Series: Mini DC/DC Step-Down (Buck) Converter - 5V @ 1A output - TSR12450
  2.1mm DC Barrel Jack: 2.1mm DC Barrel Jack with Thru-Hole Connectors (breadboardable)
